# Fritzing sketch Controlboard (saved by Fritzing 0.9.6b)
circuit board: 4cm x 5.5cm
breadboards: 1

parts:
  MTR_1 = Basic FET P-Channel [package="TO220 [THT]"]
  MTR_2 = Basic FET P-Channel [package="TO220 [THT]"]
  Sol = Basic FET P-Channel [package="TO220 [THT]"]
  BATT = Screw terminal - 2 pins [package=THT]
  MTR_2_OUT = Screw terminal - 2 pins [package=THT]
  Sol_OUT = Screw terminal - 2 pins [package=THT]
  MTR_1_OUT = Screw terminal - 2 pins [package=THT]
  C1 = Ceramic Capacitor [capacitance=100nF voltage=35V package="100 mil [THT, multilayer]"]
  MTR_1_IN = Pad [width=7.902222222222222 height=9.03111111111111 connect=center]
  MTR_2_IN = Pad [width=7.902222222222222 height=9.03111111111111 connect=center]
  SOL_IN = Pad [width=7.902222222222222 height=9.03111111111111 connect=center]
  Pad1 = Pad [width=3 height=3 connect=center]
  Pad2 = Pad [width=3 height=3 connect=center]

nets:
  N1: MTR_1.gate, MTR_1_IN.pad, Pad1.pad
  N2: MTR_1.drain, MTR_1_OUT.pin2
  N3: MTR_1.source, MTR_2.source, Sol.source, BATT.pin1, C1.1
  N4: MTR_2.gate, MTR_2_IN.pad, Pad2.pad
  N5: MTR_2.drain, MTR_2_OUT.pin2
  N6: Sol.gate, SOL_IN.pad
  N7: Sol.drain, Sol_OUT.pin2
  N8: BATT.pin2, MTR_2_OUT.pin1, Sol_OUT.pin1, MTR_1_OUT.pin1, C1.0

notes:
  If you only have one motor control
  Short pads 1 and 2, and do not
  connect MTR 2 IN
