# Fritzing sketch Flywheel driver board (saved by Fritzing 0.9.6b)
circuit board: 3.35058cm x 5.58711cm
breadboards: 1

parts:
  GND_OUT = Pad [width=7.902222222222222 height=9.03111111111111 connect=center]
  PWR_IN = Pad [width=7.902222222222222 height=9.03111111111111 connect=center]
  CTRL_IN = Pad [width=7.902222222222222 height=9.03111111111111 connect=center]
  GND_IN = Pad [width=7.902222222222222 height=9.03111111111111 connect=center]
  MTR_CTRL = Pad [width=7.902222222222222 height=9.03111111111111 connect=center]
  C1 = Capacitor [package=cap-pth-small]
  C2 = Capacitor [package=cap-pth-small]
  C3 = Capacitor [package=cap-pth-small]
  C4 = Capacitor [package=cap-pth-small]
  C5 = Capacitor [package=cap-pth-small]
  FET1 = STP16NF06 N-Channel Power MOSFET

nets:
  N1: GND_OUT.pad, GND_IN.pad, C1.2, C2.2, C3.2, C4.2, C5.2
  N2: PWR_IN.pad, C5.1, FET1.source
  N3: CTRL_IN.pad, FET1.gate
  N4: MTR_CTRL.pad, C1.1, C2.1, C3.1, C4.1, FET1.drain

custom parts:
  STP16NF06 N-Channel Power MOSFET: STP16NF06 N-channel Power MOSFET
