# Fritzing sketch Mainboard (saved by Fritzing 1.0.1rc)
circuit board: 7.16832cm x 9.39279cm
breadboards: 1

parts:
  PICO_SOCKET_HERE = ZIFSOCKET-40-6 [package=dil40-6-zif_socket]
  Mode_Switch = SS13D01
  Rev_Trig = Pushbutton [package=THT]
  Trigger = Pushbutton [package=THT]
  Safety = Pushbutton [package=THT]
  10K = Resistor [tolerance=±5% power=0.25 resistance=220 package=THT]
  10K_2 = Resistor [tolerance=±5% power=0.25 resistance=220 package=THT]
  10K_3 = Resistor [tolerance=±5% power=0.25 resistance=220 package=THT]
  10K_4 = Resistor [tolerance=±5% power=0.25 resistance=220 package=THT]
  10K_5 = Resistor [tolerance=±5% power=0.25 resistance=220 package=THT]
  10K_6 = Resistor [tolerance=±5% power=0.25 resistance=220 package=THT]
  47K = Resistor [tolerance=±5% power=0.25 resistance=220 package=THT]
  Speaker = Piezo Speaker
  100nF = Ceramic Capacitor [capacitance=100nF voltage=35V package="100 mil [THT, multilayer]"]
  100nF_2 = Ceramic Capacitor [capacitance=100nF voltage=35V package="100 mil [THT, multilayer]"]
  OUT_GND = Screw terminal - 2 pins [package=THT]
  ID_GND = Screw terminal - 2 pins [package=THT]
  SDA_SCL = Screw terminal - 2 pins [package=THT]
  OUT_GND_2 = Screw terminal - 2 pins [package=THT]
  SDA_SCL_2 = Screw terminal - 2 pins [package=THT]
  VCC_GND = Screw terminal - 2 pins [package=THT]
  TX_RX = Screw terminal - 2 pins [package=THT]

nets:
  N1: PICO_SOCKET_HERE.P$1, TX_RX.pin2
  N2: PICO_SOCKET_HERE.P$2, TX_RX.pin1
  N3: PICO_SOCKET_HERE.P$3, PICO_SOCKET_HERE.P$8, PICO_SOCKET_HERE.P$13, PICO_SOCKET_HERE.P$18, PICO_SOCKET_HERE.P$23, PICO_SOCKET_HERE.P$28, PICO_SOCKET_HERE.P$33, PICO_SOCKET_HERE.P$38, 10K.Pin_0, 10K_2.Pin_0, 10K_3.Pin_0, 10K_4.Pin_0, 10K_5.Pin_0, 10K_6.Pin_0, Speaker.pin1, 100nF.1, 100nF_2.1, OUT_GND.pin1, ID_GND.pin1, OUT_GND_2.pin1, VCC_GND.pin1
  N4: PICO_SOCKET_HERE.P$10, Mode_Switch.pin_3, 10K_3.Pin_1
  N5: PICO_SOCKET_HERE.P$11, Mode_Switch.pin_2, 10K_2.Pin_1
  N6: PICO_SOCKET_HERE.P$12, Mode_Switch.pin_1, 10K.Pin_1
  N7: PICO_SOCKET_HERE.P$15, Trigger.leg0, 10K_4.Pin_1
  N8: PICO_SOCKET_HERE.P$17, Safety.leg0, 10K_6.Pin_1
  N9: PICO_SOCKET_HERE.P$19, Rev_Trig.leg0, 10K_5.Pin_1
  N10: PICO_SOCKET_HERE.P$20, Speaker.pin2
  N11: PICO_SOCKET_HERE.P$21, SDA_SCL_2.pin2
  N12: PICO_SOCKET_HERE.P$22, SDA_SCL_2.pin1
  N13: PICO_SOCKET_HERE.P$24, SDA_SCL.pin2
  N14: PICO_SOCKET_HERE.P$25, SDA_SCL.pin1
  N15: PICO_SOCKET_HERE.P$27, OUT_GND_2.pin2
  N16: PICO_SOCKET_HERE.P$29, OUT_GND.pin2
  N17: PICO_SOCKET_HERE.P$31, PICO_SOCKET_HERE.P$36, 47K.Pin_1
  N18: PICO_SOCKET_HERE.P$32, 47K.Pin_0, ID_GND.pin2
  N19: PICO_SOCKET_HERE.P$39, Mode_Switch.pin_4, Rev_Trig.leg1, Trigger.leg1, Safety.leg1, 100nF.0, 100nF_2.0, VCC_GND.pin2

notes:
  UART
  Int i2c
  SmartBus
  Mtr Ctrl
  Sol Ctrl
  Rev. 1.0.3
  Made for TAFY

custom parts:
  SS13D01: Side-actuated SPDT slide switch, as used on the Arduino Pro
