# Fritzing sketch Mainboard_v0.0.1 (saved by Fritzing 0.9.6b)
circuit board: 7.56939cm x 15.2887cm
breadboards: 1

parts:
  U1 = ZIFSOCKET-40-6 [package=dil40-6-zif_socket]
  J1 = Piezo Speaker
  R2 = Resistor [tolerance=±5% power=0.25 resistance=220 package=THT]
  S1 = SWITCH-MOMENTARY-2 [package=reed_switch_pth]
  LED1 = LED - 3mm [color="Red (633nm)" current=0.030 package="3 mm [THT]"]
  R3 = Resistor [tolerance=±5% power=0.25 resistance=220 package=THT]

nets (from the pcb view):
  N1: U1.P$3, U1.P$8, U1.P$38, J1.pin1, LED1.anode
  N2: U1.P$7, J1.pin2
  N3: U1.P$13, U1.P$28, R2.Pin_1
  N4: U1.P$16, R3.Pin_1
  N5: U1.P$18, U1.P$23
  N6: U1.P$34, R2.Pin_0, S1.1
  N7: U1.P$36, S1.2
  N8: LED1.cathode, R3.Pin_0
