# Fritzing sketch Mainboard_v0.0.2 (saved by Fritzing 0.9.6b)
circuit board: 4.88263cm x 15.0185cm
breadboards: 1

parts:
  GND_OUT = Pad [width=7.902222222222222 height=9.03111111111111 connect=center]
  12V_IN = Pad [width=7.902222222222222 height=9.03111111111111 connect=center]
  12V_Indc = Inductor [package="400 mil [THT]"]
  C1 = Capacitor [package=cap-pth-5mm]
  12V_OUT = Pad [width=7.902222222222222 height=9.03111111111111 connect=center]
  R1 = Resistor [tolerance=±5% power=0.25 resistance=220 package=THT]
  R2 = Resistor [tolerance=±5% power=0.25 resistance=220 package=THT]
  5v_Indc = Inductor [package="400 mil [THT]"]
  C2 = Capacitor [package=cap-pth-5mm]
  5V_OUT = Pad [width=7.902222222222222 height=9.03111111111111 connect=center]
  5V_REG = LD33 Low-Dropout Voltage Regulator
  GND_IN_1 = Pad [width=7.902222222222222 height=9.03111111111111 connect=center]
  R3 = Resistor [tolerance=±5% power=0.25 resistance=220 package=THT]
  R4 = Resistor [tolerance=±5% power=0.25 resistance=220 package=THT]
  3_3v_Indc = Inductor [package="400 mil [THT]"]
  C3 = Capacitor [package=cap-pth-5mm]
  3_3V_REG = LD33 Low-Dropout Voltage Regulator
  3_3V_OUT = Pad [width=7.902222222222222 height=9.03111111111111 connect=center]
  GND_IN_2 = Pad [width=7.902222222222222 height=9.03111111111111 connect=center]
  GND_IN_3 = Pad [width=7.902222222222222 height=9.03111111111111 connect=center]
  S1 = SWITCH-MOMENTARY-2 [package=tactile-switch-1101ne]
  FET1 = STP16NF06 N-Channel Power MOSFET
  J1 = Piezo Speaker
  INT_SDA = Pad [width=7.902222222222222 height=9.03111111111111 connect=center]
  INT_SCL = Pad [width=7.902222222222222 height=9.03111111111111 connect=center]
  SB_SCL = Pad [width=7.902222222222222 height=9.03111111111111 connect=center]
  SB_SDA = Pad [width=7.902222222222222 height=9.03111111111111 connect=center]
  PICO_SOCKET_HERE = ZIFSOCKET-40-6 [package=dil40-6-zif_socket]
  SB_ID = Pad [width=7.902222222222222 height=9.03111111111111 connect=center]
  FLYWHEEL = Pad [width=7.902222222222222 height=9.03111111111111 connect=center]
  UART_TX = Pad [width=7.902222222222222 height=9.03111111111111 connect=center]
  UART_RX = Pad [width=7.902222222222222 height=9.03111111111111 connect=center]

nets:
  GND: GND_OUT.pad, C1.2, R2.Pin_1, C2.2, 5V_REG.GND, GND_IN_1.pad, R3.Pin_1, 3_3V_REG.GND, GND_IN_2.pad, GND_IN_3.pad, J1.pin1, PICO_SOCKET_HERE.P$3, PICO_SOCKET_HERE.P$8, PICO_SOCKET_HERE.P$13, PICO_SOCKET_HERE.P$18, PICO_SOCKET_HERE.P$23, PICO_SOCKET_HERE.P$28, PICO_SOCKET_HERE.P$33, PICO_SOCKET_HERE.P$38
  N1: 12V_IN.pad, 12V_Indc.pin_1
  N2: 12V_Indc.pin_0, C1.1, 12V_OUT.pad, R1.Pin_1
  N3: R1.Pin_0, R2.Pin_0, 5v_Indc.pin_0
  N4: 5v_Indc.pin_1, C2.1, 5V_REG.Vin
  N5: 5V_OUT.pad, 5V_REG.Vout, R4.Pin_1, FET1.source
  N6: R3.Pin_0, R4.Pin_0, 3_3v_Indc.pin_1
  N7: 3_3v_Indc.pin_0, C3.2
  N8: C3.1, 3_3V_REG.Vin
  N9: 3_3V_REG.Vout, 3_3V_OUT.pad, PICO_SOCKET_HERE.P$39
  N10: S1.1, PICO_SOCKET_HERE.P$36
  N11: S1.2, PICO_SOCKET_HERE.P$34
  N12: FET1.gate, PICO_SOCKET_HERE.P$20
  N13: FET1.drain, J1.pin2
  N14: INT_SDA.pad, PICO_SOCKET_HERE.P$24
  N15: INT_SCL.pad, PICO_SOCKET_HERE.P$25
  N16: SB_SCL.pad, PICO_SOCKET_HERE.P$27
  N17: SB_SDA.pad, PICO_SOCKET_HERE.P$26
  N18: PICO_SOCKET_HERE.P$12, FLYWHEEL.pad
  N19: PICO_SOCKET_HERE.P$21, UART_TX.pad
  N20: PICO_SOCKET_HERE.P$22, UART_RX.pad
  N21: PICO_SOCKET_HERE.P$31, SB_ID.pad

custom parts:
  STP16NF06 N-Channel Power MOSFET: STP16NF06 N-channel Power MOSFET
