# Fritzing sketch Battery Holder (saved by Fritzing 1.0.1rc)
circuit board: 6.14009cm x 10.3753cm
breadboards: 1

parts:
  Bat1 = battery_holder_dual_18650 [part_number=TBH-18650-2A-P]
  Bat2 = battery_holder_dual_18650 [part_number=TBH-18650-2A-P]
  J1 = Screw terminal - 2 pins [package=THT]
  J2 = Screw terminal - 2 pins [package=THT]

nets:
  N1: Bat1.+#1, Bat2.+#2, J1.pin2
  N2: Bat1.+#2, J1.pin1
  N3: Bat2.+#0, J2.pin2
  N4: Bat2.+#1, Bat2.+#3, J2.pin1

notes:
  GND 4.2v 8.4v 12.6v
  Bat3
  OUT TO BMS
  + Up Here
  - Down Here

custom parts:
  battery_holder_dual_18650: TBH-18650-2A-P dual 18650 battery holder.
