# Fritzing sketch Mainboard (saved by Fritzing 1.0.1rc)
circuit board: 7.16832cm x 10.4449cm
breadboards: 1

parts:
  PICO_SOCKET_HERE = ZIFSOCKET-40-6 [package=dil40-6-zif_socket]
  Mode_Switch = SS13D01
  Rev_Trig = Pushbutton [package=THT]
  Trigger = Pushbutton [package=THT]
  Safety = Pushbutton [package=THT]
  10K = Resistor [tolerance=±5% power=0.25 resistance=220 package=THT]
  10K_2 = Resistor [tolerance=±5% power=0.25 resistance=220 package=THT]
  10K_3 = Resistor [tolerance=±5% power=0.25 resistance=220 package=THT]
  10K_4 = Resistor [tolerance=±5% power=0.25 resistance=220 package=THT]
  10K_5 = Resistor [tolerance=±5% power=0.25 resistance=220 package=THT]
  10K_6 = Resistor [tolerance=±5% power=0.25 resistance=220 package=THT]
  47K = Resistor [tolerance=±5% power=0.25 resistance=220 package=THT]
  Speaker = Piezo Speaker
  100nF = Ceramic Capacitor [capacitance=100nF voltage=35V package="100 mil [THT, multilayer]"]
  100nF_2 = Ceramic Capacitor [capacitance=100nF voltage=35V package="100 mil [THT, multilayer]"]
  ID_GND = Screw terminal - 2 pins [package=THT]
  SDA_SCL = Screw terminal - 2 pins [package=THT]
  SDA_SCL_2 = Screw terminal - 2 pins [package=THT]
  VCC_GND = Screw terminal - 2 pins [package=THT]
  TX_RX = Screw terminal - 2 pins [package=THT]
  PWM_REV_FWD = screw terminal, 3 pins
  PWM_REV_FWD_2 = screw terminal, 3 pins
  Bat_Ind_Charge = Screw terminal - 2 pins [package=THT]
  R1 = Resistor [tolerance=±5% power=0.25 resistance=220 package=THT]
  SAFETY_PWM_ENABLE = screw terminal, 3 pins

nets:
  N1: PICO_SOCKET_HERE.P$1, TX_RX.pin2
  N2: PICO_SOCKET_HERE.P$2, TX_RX.pin1
  N3: PICO_SOCKET_HERE.P$3, PICO_SOCKET_HERE.P$8, PICO_SOCKET_HERE.P$13, PICO_SOCKET_HERE.P$18, PICO_SOCKET_HERE.P$23, PICO_SOCKET_HERE.P$28, PICO_SOCKET_HERE.P$33, PICO_SOCKET_HERE.P$38, 10K.Pin_0, 10K_2.Pin_0, 10K_3.Pin_0, 10K_4.Pin_0, 10K_5.Pin_0, 10K_6.Pin_0, Speaker.pin1, 100nF.1, 100nF_2.1, ID_GND.pin1, VCC_GND.pin1, R1.Pin_0
  N4: PICO_SOCKET_HERE.P$4, PWM_REV_FWD_2.pin1
  N5: PICO_SOCKET_HERE.P$5, PWM_REV_FWD_2.pin2
  N6: PICO_SOCKET_HERE.P$6, PWM_REV_FWD_2.pin3
  N7: PICO_SOCKET_HERE.P$7, PWM_REV_FWD.pin1
  N8: PICO_SOCKET_HERE.P$9, PWM_REV_FWD.pin2
  N9: PICO_SOCKET_HERE.P$10, PWM_REV_FWD.pin3
  N10: PICO_SOCKET_HERE.P$11, Mode_Switch.pin_3, 10K_3.Pin_1
  N11: PICO_SOCKET_HERE.P$12, Mode_Switch.pin_2, 10K_2.Pin_1
  N12: PICO_SOCKET_HERE.P$14, Mode_Switch.pin_1, 10K.Pin_1
  N13: PICO_SOCKET_HERE.P$15, Trigger.leg0, 10K_4.Pin_1
  N14: PICO_SOCKET_HERE.P$16, Safety.leg0, 10K_6.Pin_1, SAFETY_PWM_ENABLE.pin3
  N15: PICO_SOCKET_HERE.P$17, Rev_Trig.leg0, 10K_5.Pin_1
  N16: PICO_SOCKET_HERE.P$19, Bat_Ind_Charge.pin1
  N17: PICO_SOCKET_HERE.P$20, Speaker.pin2
  N18: PICO_SOCKET_HERE.P$21, SDA_SCL_2.pin2
  N19: PICO_SOCKET_HERE.P$22, SDA_SCL_2.pin1
  N20: PICO_SOCKET_HERE.P$24, SDA_SCL.pin2
  N21: PICO_SOCKET_HERE.P$25, SDA_SCL.pin1
  N22: PICO_SOCKET_HERE.P$26, SAFETY_PWM_ENABLE.pin2
  N23: PICO_SOCKET_HERE.P$27, SAFETY_PWM_ENABLE.pin1
  N24: PICO_SOCKET_HERE.P$31, PICO_SOCKET_HERE.P$36, 47K.Pin_1
  N25: PICO_SOCKET_HERE.P$32, 47K.Pin_0, ID_GND.pin2
  N26: PICO_SOCKET_HERE.P$34, Bat_Ind_Charge.pin2, R1.Pin_1
  N27: PICO_SOCKET_HERE.P$39, Mode_Switch.pin_4, Rev_Trig.leg1, Trigger.leg1, Safety.leg1, 100nF.0, 100nF_2.0, VCC_GND.pin2

notes:
  UART
  Int i2c
  SmartBus
  Mtr Ctrl 2
  Sol Ctrl
  Rev. 1.0.7
  Made for TAFY
  Mtr Ctrl 1

custom parts:
  SS13D01: Side-actuated SPDT slide switch, as used on the Arduino Pro
