# Fritzing sketch Motor Controlboard - Half Bridge (saved by Fritzing 1.0.1rc)
circuit board: 6.1cm x 9.25cm
breadboards: 1

parts:
  PNP = Basic FET N-Channel-flat [package="TO220 [THT]"]
  U1 = DIODE-ZENER [package=diode-zener]
  U2 = DIODE-ZENER [package=diode-zener]
  MOTOR_IN = screw terminal, 2 pins
  SOL_SAFETY = screw terminal, 2 pins
  VCC_GND = screw terminal, 2 pins
  SOL_OUT = screw terminal, 2 pins
  MOTOR_TWO_OUT = screw terminal, 2 pins
  MOTOR_ONE_OUT = screw terminal, 2 pins
  PNP_2 = Basic FET N-Channel-flat [package="TO220 [THT]"]
  U3 = DIODE-ZENER [package=diode-zener]
  U4 = DIODE-ZENER [package=diode-zener]
  NPN = Basic FET N-Channel-flat [package="TO220 [THT]"]
  U5 = DIODE-ZENER [package=diode-zener]
  Q6 = PNP-Transistor [package="TO92 [THT]"]
  Q7 = PNP-Transistor [package="TO92 [THT]"]
  Q8 = PNP-Transistor [package="TO92 [THT]"]
  R1 = Resistor [tolerance=±5% power=0.25 resistance=220 package=THT]
  R2 = Resistor [tolerance=±5% power=0.25 resistance=220 package=THT]
  R3 = Resistor [tolerance=±5% power=0.25 resistance=220 package=THT]
  R4 = Resistor [tolerance=±5% power=0.25 resistance=220 package=THT]
  NPN_2 = Basic FET N-Channel-flat [package="TO220 [THT]"]
  NPN_3 = Basic FET N-Channel-flat [package="TO220 [THT]"]
  R5 = Resistor [tolerance=±5% power=0.25 resistance=220 package=THT]
  R6 = Resistor [tolerance=±5% power=0.25 resistance=220 package=THT]
  R7 = Resistor [tolerance=±5% power=0.25 resistance=220 package=THT]
  R8 = Resistor [tolerance=±5% power=0.25 resistance=220 package=THT]
  C1 = Ceramic Capacitor [capacitance=100nF voltage=35V package="100 mil [THT, multilayer]"]
  Q9 = NPN-Transistor [package="TO92 [THT]"]
  Q10 = NPN-Transistor [package="TO92 [THT]"]
  R9 = Resistor [tolerance=±5% power=0.25 resistance=220 package=THT]
  R10 = Resistor [tolerance=±5% power=0.25 resistance=220 package=THT]
  R11 = Resistor [tolerance=±5% power=0.25 resistance=220 package=THT]
  R12 = Resistor [tolerance=±5% power=0.25 resistance=220 package=THT]

nets:
  N1: PNP.1, Q9.E, R11.Pin_1
  N2: PNP.2, U1.C, MOTOR_ONE_OUT.pin2
  N3: PNP.3, U1.A, VCC_GND.pin2, SOL_OUT.pin2, PNP_2.3, U3.A, C1.0, R11.Pin_0, R12.Pin_0
  N4: U2.C, VCC_GND.pin1, U4.C, NPN.2, U5.C, R1.Pin_1, R2.Pin_1, R3.Pin_1, R4.Pin_1, NPN_2.2, NPN_3.2, R5.Pin_1, R6.Pin_1, R7.Pin_1, R8.Pin_0, C1.1, Q9.C, Q10.C, R9.Pin_1, R10.Pin_1
  N5: U2.A, MOTOR_ONE_OUT.pin1, NPN_3.3
  N6: MOTOR_IN.pin1, Q7.C
  N7: MOTOR_IN.pin2, Q6.C
  N8: SOL_SAFETY.pin1, Q6.B, Q7.B, Q8.B, R5.Pin_0, R6.Pin_0, R7.Pin_0
  N9: SOL_SAFETY.pin2, Q8.C
  N10: SOL_OUT.pin1, NPN.3, U5.A
  N11: MOTOR_TWO_OUT.pin1, U4.A, NPN_2.3
  N12: MOTOR_TWO_OUT.pin2, PNP_2.2, U3.C
  N13: PNP_2.1, Q10.E, R12.Pin_1
  N14: NPN.1, Q8.E, R8.Pin_1
  N15: Q6.E, Q9.B, R9.Pin_0
  N16: Q7.E, Q10.B, R10.Pin_0
  N17: R1.Pin_0, R2.Pin_0, NPN_3.1
  N18: R3.Pin_0, R4.Pin_0, NPN_2.1

notes:
  Made for TAFY
  v0.4.0
  Motor Controlboard
  half-H-bridge version

custom parts:
  Basic FET N-Channel-flat: MOSFET N-Channel Transistor lying flat on PCB. 16.7mm from mounting hole centre to leg hole centres.
