# Fritzing sketch Power Supply (saved by Fritzing 1.0.1rc)
circuit board: 9.09339cm x 11.6547cm
breadboards: 1

parts:
  M1 = RioRand LM2596
  M2 = RioRand LM2596
  M3 = RioRand LM2596
  C1 = Capacitor [package=cap-pth-small-kit]
  C2 = Capacitor [package=cap-pth-small-kit]
  C3 = Capacitor [package=cap-pth-small-kit]
  C4 = Capacitor [package=cap-pth-small-kit]
  C5 = Capacitor [package=cap-pth-small-kit]
  C6 = Capacitor [package=cap-pth-small-kit]
  C7 = Capacitor [package=cap-pth-small-kit]
  C8 = Capacitor [package=cap-pth-small-kit]
  C9 = Capacitor [package=cap-pth-small-kit]
  GND_Vbat = Screw terminal - 2 pins [package=THT]
  5v_-_1A = Screw terminal - 2 pins [package=THT]
  5v_-_750mA = Screw terminal - 2 pins [package=THT]
  3_3v_-_250mA = Screw terminal - 2 pins [package=THT]
  PPTC = Resistor [tolerance=±5% power=0.25 resistance=220 package=THT]
  PPTC1 = Resistor [tolerance=±5% power=0.25 resistance=220 package=THT]
  PPTC2 = Resistor [tolerance=±5% power=0.25 resistance=220 package=THT]
  PPTC3 = Resistor [tolerance=±5% power=0.25 resistance=220 package=THT]
  LD1117V33 = Voltage Regulator-flat [package="TO220 [THT]"]
  C10 = Capacitor [package=cap-pth-small-kit]
  47K_Ohms = Resistor [tolerance=±5% power=0.25 resistance=47k package=THT]
  100_Ohm = Resistor [tolerance=±5% power=0.25 resistance=300 package=THT]
  Bat_Ind_Charge = Screw terminal - 2 pins [package=THT]
  Vin_GND_Charge_IN = screw terminal, 3 pins

nets (from the pcb view):
  N1: M1.Pin_1, PPTC2.Pin_1
  N2: M1.Pin_2, M2.Pin_2, M3.Pin_2, C1.2, C2.2, C3.2, C4.1, C5.1, C6.1, PPTC3.Pin_0, 47K_Ohms.Pin_0, Vin_GND_Charge_IN.pin2
  N3: M1.Pin_3, C7.1, 3_3v_-_250mA.pin2
  N4: M1.Pin_4, C7.2, 3_3v_-_250mA.pin1
  N5: M2.Pin_1, PPTC1.Pin_1
  N6: M2.Pin_3, C8.1, 5v_-_750mA.pin2
  N7: M2.Pin_4, C8.2, 5v_-_750mA.pin1
  N8: M3.Pin_1, PPTC.Pin_1
  N9: M3.Pin_3, C9.1, 5v_-_1A.pin2
  N10: M3.Pin_4, C9.2, 5v_-_1A.pin1
  N11: C1.1, C2.1, C3.1, C4.2, C5.2, C6.2, GND_Vbat.pin1, PPTC.Pin_0, PPTC1.Pin_0, PPTC2.Pin_0, LD1117V33.input_voltage, LD1117V33.GND, C10.1, C10.2, Vin_GND_Charge_IN.pin1, Vin_GND_Charge_IN.pin3
  N12: GND_Vbat.pin2, PPTC3.Pin_1
  N13: LD1117V33.output_voltage, 100_Ohm.Pin_0
  N14: 47K_Ohms.Pin_1, Bat_Ind_Charge.pin2
  N15: 100_Ohm.Pin_1, Bat_Ind_Charge.pin1

notes:
  LM2596 - 5v - 1A
  LM2596 - 5v - 750mA
  LM2596 - 3.3v - 250mA
  v0.1.0
  Made for TAFY

custom parts:
  Voltage Regulator-flat: DC Voltage Regulator lying flat on PCB 16.7mm from mounting hole centre to leg hole centres.
